# Fritzing sketch TemperatureAndHumidityDisplayer (saved by Fritzing 0.9.3b)
breadboards: 1

parts:
  Parte1 = Arduino Uno (Rev3)
  Parte2 = LCD1602-I2C
  Mod1 = KY-015 Temperature & Humidity Sensor Module [package="Breakout board"]
  R1 = Resistor [tolerance=±5% resistance=220 package=THT]
  R2 = Resistor [tolerance=±5% resistance=220 package=THT]
  R3 = Resistor [tolerance=±5% resistance=220 package=THT]
  LED2 = smd LED [color="Red (633nm)" package="1206 [SMD]"]
  LED3 = smd LED [color="Red (633nm)" package="1206 [SMD]"]
  LED4 = smd LED [color="Red (633nm)" package="1206 [SMD]"]

nets:
  N1: Parte1.D9_PWM, R2.Pin_1
  N2: Parte1.D10_PWM/SS, R3.Pin_1
  N3: Parte1.D11_PWM/MOSI, R1.Pin_1
  GND: Parte1.GND, Parte2.GND, Mod1.-, LED2.cathode, LED3.cathode, LED4.cathode
  N4: Parte1.A4/SDA, Parte2.SDA
  N5: Parte1.A5/SCL, Parte2.SCL
  N6: Parte1.D2, Mod1.S
  3V3: Parte1.3V3, Mod1.Vin
  5V: Parte1.5V, Parte2.VCC
  N7: R1.Pin_0, LED3.anode
  N8: R2.Pin_0, LED2.anode
  N9: R3.Pin_0, LED4.anode

custom parts:
  LCD1602-I2C: A standard character display, usually with 2x16 characters. Comes in many colors with LCM1602 IIC attached.
  KY-015 Temperature & Humidity Sensor Module: KY-015 temperature and humidity sensor module, provides a low-latency serial interface to measure humidity and temperature.

// code stored in the sketch: TemperaturSensorLM35.ino
/*
  LCD Display with I2C Interface and DHT-22 Temp/Humid Sensor
  lcd-i2c-temp-humid.ino
  Use NewLiquidCrystal Library
  Use DHT Libraries from Adafruit
  DroneBot Workshop 2018
  https://dronebotworkshop.com
*/


// Include Wire Library for I2C
#include <Wire.h>
// Include NewLiquidCrystal Library for I2C
#include <LiquidCrystal_I2C.h>


// Include DHT Libraries from Adafruit
// Dependant upon Adafruit_Sensors Library
#include "DHT.h";


// Define LCD pinout
const int en = 2, rw = 1, rs = 0, d4 = 4, d5 = 5, d6 = 6, d7 = 7, bl = 3;


// Define I2C Address - change if reqiuired
const int i2c_addr = 0x27;


// DHT-22
#define DHTPIN 2       // DHT-22 Output Pin connection
#define DHTTYPE DHT11  // DHT Type is DHT 22 (AM2302)


#define LED_PIN_RED 11
#define LED_PIN_YELLOW 10
#define LED_PIN_GREEN 9


// Define LCD display connections
LiquidCrystal_I2C lcd(i2c_addr, en, rw, rs, d4, d5, d6, d7, bl, POSITIVE);


// Define Variables
float hum;   // Stores humidity value in percent
float temp;  // Stores temperature value in Celsius


// Setup DHT sensor for normal 16mhz Arduino
DHT dht(DHTPIN, DHTTYPE);


void setup() {


  // Set display type as 16 char, 2 rows
  lcd.begin(16, 2);


  // Initialize DHT-11
  dht.begin();


  pinMode(LED_PIN_RED, OUTPUT);
  pinMode(LED_PIN_YELLOW, OUTPUT);
  pinMode(LED_PIN_GREEN, OUTPUT);
}


void loop() {
  delay(1500);  // Delay so DHT-11 sensor can stabalize


  hum = dht.readHumidity();      // Get Humidity value
  temp = dht.readTemperature();  // Get Temperature value


  // Clear the display
  lcd.clear();


  // Print temperature on top line
  lcd.setCursor(0, 0);
  lcd.print("Temp: ");
  lcd.print(temp);
  lcd.print(" C");
  lcd.print((char)223);



  // Print humidity on bottom line
  lcd.setCursor(0, 1);
  lcd.print("Umid: ");
  lcd.print(hum);
  lcd.print(" %");


  if (hum >= 60 || hum <= 20) {
    digitalWrite(LED_PIN_RED, HIGH);
    digitalWrite(LED_PIN_YELLOW, LOW);
    digitalWrite(LED_PIN_GREEN, LOW);
  } else if (hum >= 50 || hum <= 30) {
    digitalWrite(LED_PIN_RED, LOW);
    digitalWrite(LED_PIN_YELLOW, HIGH);
    digitalWrite(LED_PIN_GREEN, LOW);
  } else {
    digitalWrite(LED_PIN_RED, LOW);
    digitalWrite(LED_PIN_YELLOW, LOW);
    digitalWrite(LED_PIN_GREEN, HIGH);
  }
}
